# Fritzing sketch TPS Pin assigment (saved by Fritzing 0.9.4)
breadboards: 2

parts:
  Mod1 = Raspberry Pi Pico
  LED1 = smd LED [color="Yellow (585nm)" package="1206 [SMD]"]
  LED2 = smd LED [color="Yellow (585nm)" package="1206 [SMD]"]
  LED3 = smd LED [color="Yellow (585nm)" package="1206 [SMD]"]
  LED4 = smd LED [color="Yellow (585nm)" package="1206 [SMD]"]
  R1 = Resistor [tolerance=±1% resistance=1.4k package="0805 [SMD]"]
  R2 = Resistor [tolerance=±1% resistance=1.4k package="0805 [SMD]"]
  R3 = Resistor [tolerance=±1% resistance=1.4k package="0805 [SMD]"]
  R4 = Resistor [tolerance=±1% resistance=1.4k package="0805 [SMD]"]
  S1 = Pushbutton [package="[THT]"]
  S2 = Pushbutton [package="[THT]"]
  S3 = Pushbutton [package="[THT]"]
  R5 = Rotary Potentiometer (Small) [maximum_resistance=100kΩ package=THT]
  R6 = Rotary Potentiometer (Small) [maximum_resistance=100kΩ package=THT]
  S4 = Pushbutton [package="[THT]"]
  S5 = Pushbutton [package="[THT]"]
  S6 = Pushbutton [package="[THT]"]
  S7 = Pushbutton [package="[THT]"]
  LED5 = smd LED [color="Green (560nm)" package="1206 [SMD]"]
  LED6 = smd LED [color="Green (560nm)" package="1206 [SMD]"]
  LED7 = smd LED [color="Green (560nm)" package="1206 [SMD]"]
  LED8 = smd LED [color="Green (560nm)" package="1206 [SMD]"]
  R7 = Resistor [tolerance=±1% resistance=1.4k package="0805 [SMD]"]
  R8 = Resistor [tolerance=±1% resistance=1.4k package="0805 [SMD]"]
  R9 = Resistor [tolerance=±1% resistance=1.4k package="0805 [SMD]"]
  R10 = Resistor [tolerance=±1% resistance=1.4k package="0805 [SMD]"]
  J1 = Piezo Speaker
  R11 = Resistor [tolerance=±1% resistance=1.4k package="0805 [SMD]"]

nets:
  N1: Mod1.pin_3, Mod1.pin_8, Mod1.pin_13, Mod1.pin_18, Mod1.pin_23, Mod1.pin_28, Mod1.pin_33, Mod1.pin_38, Mod1.pin_42, LED1.cathode, LED2.cathode, LED3.cathode, LED4.cathode, S1.Pin_1, S1.Pin_2, S2.Pin_1, S2.Pin_2, S3.Pin_1, S3.Pin_2, R5.leg1, R6.leg1, S4.Pin_1, S4.Pin_2, S5.Pin_1, S5.Pin_2, S6.Pin_1, S6.Pin_2, S7.Pin_1, S7.Pin_2, LED5.cathode, LED6.cathode, LED7.cathode, LED8.cathode, J1.pin1
  N2: Mod1.pin_4, R4.Pin_1
  N3: Mod1.pin_5, R2.Pin_1
  N4: Mod1.pin_6, R3.Pin_1
  N5: Mod1.pin_7, R1.Pin_1
  N6: Mod1.pin_9, S6.Pin_3, S6.Pin_4
  N7: Mod1.pin_10, S1.Pin_3, S1.Pin_4
  N8: Mod1.pin_11, S5.Pin_3, S5.Pin_4
  N9: Mod1.pin_12, S4.Pin_3, S4.Pin_4
  N10: Mod1.pin_14, S3.Pin_3, S3.Pin_4
  N11: Mod1.pin_15, S2.Pin_3, S2.Pin_4
  N12: Mod1.pin_21, R7.Pin_1
  N13: Mod1.pin_22, R8.Pin_1
  N14: Mod1.pin_24, R11.Pin_1
  N15: Mod1.pin_26, R9.Pin_1
  N16: Mod1.pin_27, R10.Pin_1
  N17: Mod1.pin_30, S7.Pin_3, S7.Pin_4
  N18: Mod1.pin_31, R5.wiper
  N19: Mod1.pin_32, R6.wiper
  N20: Mod1.pin_36, R5.leg2, R6.leg2
  N21: LED1.anode, R1.Pin_0
  N22: LED2.anode, R2.Pin_0
  N23: LED3.anode, R3.Pin_0
  N24: LED4.anode, R4.Pin_0
  N25: LED5.anode, R7.Pin_0
  N26: LED6.anode, R9.Pin_0
  N27: LED7.anode, R10.Pin_0
  N28: LED8.anode, R8.Pin_0
  N29: J1.pin2, R11.Pin_0

notes:
  PWM
  1  2  3  4
  4  3  2  1
  Input
  Output
  Analog
  1   2
  PRG RES SEL

custom parts:
  Raspberry Pi Pico: Raspberry Pi Pico. Based around the RP2040 microcontroller the Pico is a low cost microcontroller device bringing Raspberry Pi quality, cost, and easy of use to the microcontroller space. Jan 2021, Split part in to two versions: tht (this one) and SMD. This one will drill holes for a .1 in header in pcb to allow plugging in the module as well as providing pads to solder the module to the top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
